// Logisim project Divider.circ as structural Verilog: 2 circuits, main circuit main
module main (
  input  [5:0] Numerator,
  input  [5:0] Denominator,
  output [5:0] Quotient,
  output [5:0] Remainder,
  output Divide_by_Zero__Error
);

  wire comparator_1_lt, pull_resistor_2_node, pull_resistor_3_node, pull_resistor_4_node,
       pull_resistor_5_node, pull_resistor_6_node, pull_resistor_7_node, subtractor_1_bout,
       subtractor_2_bout, subtractor_3_bout, subtractor_4_bout, subtractor_5_bout, subtractor_6_bout,
       zero6_2_zero, zero6_3_zero, zero6_4_zero, zero6_5_zero, zero6_6_zero, zero6_7_zero;
  wire [2:0] pull_resistor_1_node, pull_resistor_1_node_2;
  wire [5:0] and_6_out, multiplexer_1_out, multiplexer_2_out, multiplexer_3_out, multiplexer_4_out,
       multiplexer_6_out, subtractor_1_out, subtractor_2_out, subtractor_3_out, subtractor_4_out,
       subtractor_5_out, subtractor_6_out;

  Comparator #(.width(6), .mode("unsigned")) comparator_1 (
    .a(Numerator), .b(Denominator), .lt(comparator_1_lt));  // open: gt, eq
  Pull_Resistor pull_resistor_1 (.node({pull_resistor_1_node_2, pull_resistor_1_node}));
  Zero6 zero6_1 (.A(Denominator), .Zero(Divide_by_Zero__Error));
  Pull_Resistor pull_resistor_2 (.node(pull_resistor_2_node));
  Subtractor #(.width(6)) subtractor_1 (
    .a(Numerator), .b({Denominator[0], pull_resistor_1_node_2, pull_resistor_1_node[2:1]}),
    .out(subtractor_1_out), .bin(pull_resistor_2_node), .bout(subtractor_1_bout));
  and and_1 (and_6_out[5], ~subtractor_1_bout, zero6_2_zero);  // AND_Gate
  Zero6 zero6_2 (.A({1'b0, Denominator[5:1]}), .Zero(zero6_2_zero));
  Multiplexer #(.width(6), .enable("false")) multiplexer_1 (
    .in0(Numerator), .in1(subtractor_1_out), .out(multiplexer_1_out), .sel(and_6_out[5]));
  Pull_Resistor pull_resistor_3 (.node(pull_resistor_3_node));
  Subtractor #(.width(6)) subtractor_2 (
    .a(multiplexer_1_out), .b({Denominator[1:0], pull_resistor_1_node_2, pull_resistor_1_node[2]}),
    .out(subtractor_2_out), .bin(pull_resistor_3_node), .bout(subtractor_2_bout));
  Zero6 zero6_3 (.A({2'b00, Denominator[5:2]}), .Zero(zero6_3_zero));
  and and_2 (and_6_out[4], ~subtractor_2_bout, zero6_3_zero);  // AND_Gate
  Multiplexer #(.width(6), .enable("false")) multiplexer_2 (
    .in0(multiplexer_1_out), .in1(subtractor_2_out), .out(multiplexer_2_out), .sel(and_6_out[4]));
  Pull_Resistor pull_resistor_4 (.node(pull_resistor_4_node));
  Subtractor #(.width(6)) subtractor_3 (
    .a(multiplexer_2_out), .b({Denominator[2:0], pull_resistor_1_node_2}), .out(subtractor_3_out),
    .bin(pull_resistor_4_node), .bout(subtractor_3_bout));
  Zero6 zero6_4 (.A({3'b000, Denominator[5:3]}), .Zero(zero6_4_zero));
  and and_3 (and_6_out[3], ~subtractor_3_bout, zero6_4_zero);  // AND_Gate
  Multiplexer #(.width(6), .enable("false")) multiplexer_3 (
    .in0(multiplexer_2_out), .in1(subtractor_3_out), .out(multiplexer_3_out), .sel(and_6_out[3]));
  Pull_Resistor pull_resistor_5 (.node(pull_resistor_5_node));
  Zero6 zero6_5 (.A({4'b0000, Denominator[5:4]}), .Zero(zero6_5_zero));
  Subtractor #(.width(6)) subtractor_4 (
    .a(multiplexer_3_out), .b({Denominator[3:0], pull_resistor_1_node_2[2:1]}), .out(subtractor_4_out),
    .bin(pull_resistor_5_node), .bout(subtractor_4_bout));
  and and_4 (and_6_out[2], ~subtractor_4_bout, zero6_5_zero);  // AND_Gate
  Multiplexer #(.width(6), .enable("false")) multiplexer_4 (
    .in0(multiplexer_3_out), .in1(subtractor_4_out), .out(multiplexer_4_out), .sel(and_6_out[2]));
  Pull_Resistor pull_resistor_6 (.node(pull_resistor_6_node));
  Zero6 zero6_6 (.A({{5{1'b0}}, Denominator[5]}), .Zero(zero6_6_zero));
  Subtractor #(.width(6)) subtractor_5 (
    .a(multiplexer_4_out), .b({Denominator[4:0], pull_resistor_1_node_2[2]}), .out(subtractor_5_out),
    .bin(pull_resistor_6_node), .bout(subtractor_5_bout));
  and and_5 (and_6_out[1], ~subtractor_5_bout, zero6_6_zero);  // AND_Gate
  Multiplexer #(.width(6), .enable("false")) multiplexer_5 (
    .in0(and_6_out), .in1({6{1'b0}}), .out(Quotient), .sel(comparator_1_lt));
  Multiplexer #(.width(6), .enable("false")) multiplexer_6 (
    .in0(multiplexer_4_out), .in1(subtractor_5_out), .out(multiplexer_6_out), .sel(and_6_out[1]));
  Pull_Resistor pull_resistor_7 (.node(pull_resistor_7_node));
  Subtractor #(.width(6)) subtractor_6 (
    .a(multiplexer_6_out), .b(Denominator), .out(subtractor_6_out), .bin(pull_resistor_7_node),
    .bout(subtractor_6_bout));
  and and_6 (and_6_out[0], ~subtractor_6_bout, zero6_7_zero);  // AND_Gate
  Zero6 zero6_7 (.A({6{1'b0}}), .Zero(zero6_7_zero));
  Multiplexer #(.width(6), .enable("false")) multiplexer_7 (
    .in0(multiplexer_6_out), .in1(subtractor_6_out), .out(Remainder), .sel(and_6_out[0]));

  // Notes on the sheet:
  //   If Zero, Quotient will contain all 1's. Remainder will be Numerator.
  //   If N<D, the Quotient will be 0. Remainder will be Numerator
  //   6 Bit Divider Circuit
endmodule

// Z6
module Zero6 (
  input  [5:0] A,
  output Zero
);

  nor nor_1 (Zero, A[0], A[1], A[2], A[3], A[4], A[5]);

  // Notes on the sheet:
  //   Is Input Zero?
endmodule
