// Logisim project Parity Checker.circ as structural Verilog: 1 circuit, main circuit main
module main (
  input  A0,
  input  A1,
  input  A2,
  input  A3,
  input  A4,
  input  A5,
  output X
);

  wire xor_1_out, xor_2_out, xor_3_out, xor_4_out;

  xor xor_1 (xor_1_out, A0, A1);
  xor xor_2 (xor_2_out, xor_1_out, A2);
  xor xor_3 (xor_3_out, xor_2_out, A3);
  xor xor_4 (xor_4_out, xor_3_out, A4);
  xor xor_5 (X, xor_4_out, A5);

  // Notes on the sheet:
  //   0 FOR EVEN PARITY OR 1 FOR ODD PARITY
endmodule
